# Fritzing sketch 2.1.1 (saved by Fritzing 0.9.5d)
breadboards: 1

parts:
  T-Cobbler1 = T-Cobbler
  S1 = Pushbutton [package="[THT]"]
  S2 = Pushbutton [package="[THT]"]
  S3 = Pushbutton [package="[THT]"]
  R1 = Resistor [tolerance=±5% resistance=10k package=THT]
  R3 = Resistor [tolerance=±5% resistance=10k package=THT]
  R4 = Resistor [tolerance=±5% resistance=10k package=THT]

nets:
  N1: T-Cobbler1.3V3#8, R1.Pin_0, R4.Pin_0
  N2: T-Cobbler1.GND#12, S1.Pin_1, S1.Pin_2, S2.Pin_1, S2.Pin_2
  N3: T-Cobbler1.GPIO18, S1.Pin_3, S1.Pin_4, R1.Pin_1
  N4: T-Cobbler1.GPIO23, S2.Pin_3, S2.Pin_4, R3.Pin_1
  N5: T-Cobbler1.GND#29, S3.Pin_3, S3.Pin_4, R4.Pin_1
  N6: S3.Pin_1, S3.Pin_2

custom parts:
  T-Cobbler: T-Cobbler for raspberry Pi 5 & earlier
